# Fritzing sketch wiring_sch (saved by Fritzing 0.9.5d)

parts:
  Part1 = Adafruit PCA9685 PWM/Servo Breakout [part_number=815]
  Part2 = Arduino Nano (Rev3.0)
  J1 = Basic Servo

nets:
  N1: Part1.PWM0, J1.pulse
  N2: Part1.5.0V, J1.vcc
  GND: Part1.GND, Part2.GND, J1.gnd
  VCC: Part1.VCC, Part2.5V
  N3: Part1.SDA, Part2.A4
  N4: Part1.SCL, Part2.A5

custom parts:
  Adafruit PCA9685 PWM/Servo Breakout: Using only two pins, control 16 free-running PWM outputs! I2C-controlled PWM driver with a built in clock. Unlike the TLC5940 family, you do not need to continuously send it signal tying up your microcontroller, its completely free running! 5V compliant, which means you can control it from a 3.3V microcontroller and still safely drive up to 6V outputs (this is good for when you want to control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
